# Fritzing sketch dashboard (saved by Fritzing 0.9.3b)
breadboards: 1

parts:
  S1 = Pushbutton [package="[THT]"]
  U1 = ESP8266 NodeMCU LoLin module
  Часть1 = LCD1602-I2C
  R1 = Resistor [tolerance=±5% resistance=10k package=THT]

nets:
  N1: S1.Pin_1, S1.Pin_2, U1.3V3
  N2: S1.Pin_3, S1.Pin_4, U1.D7, R1.Pin_1
  N3: U1.D0, Часть1.SCL
  N4: U1.D1, Часть1.SDA
  GND: U1.GND, Часть1.GND, R1.Pin_0
  N5: U1.VU, Часть1.VCC

custom parts:
  ESP8266 NodeMCU LoLin module: ESP8266 based NodeMCU
  LCD1602-I2C: A standard character display, usually with 2x16 characters. Comes in many colors with LCM1602 IIC attached.
